# Fritzing sketch MACHINE GUN (saved by Fritzing 0.9.6b)
circuit board: 8.46667cm x 5.64444cm

parts:
  R2 = Resistor [tolerance=±5% power=0.25 resistance=33k package=THT]
  R1 = Resistor [tolerance=±5% power=0.25 resistance=100k package=THT]
  C1 = Ceramic Capacitor [capacitance=10nF voltage=35V package="100 mil [THT, multilayer]"]
  C2 = Ceramic Capacitor [capacitance=10nF voltage=35V package="100 mil [THT, multilayer]"]
  U1 = 555 Timer [package="DIP8 [THT]"]
  C3 = Ceramic Capacitor [capacitance=10µF voltage=35V package="100 mil [THT, multilayer]"]
  C4 = Ceramic Capacitor [capacitance=10µF voltage=35V package="100 mil [THT, multilayer]"]
  SPKR1 = Loudspeaker
  Q1 = NPN-Transistor [package="TO92 [THT]"]
  V1 = DC Power [voltage=6V]

nets:
  N1: R2.Pin_0, U1.Output, U1.Reset, U1.Vcc_Supply_Voltage, C3.0, C3.1, C4.0, SPKR1.pin2, Q1.E
  N2: R2.Pin_1, C1.1, U1.Trigger
  N3: R1.Pin_0, C4.1, Q1.B
  N4: R1.Pin_1, C1.0, C2.0, U1.Ground
  N5: C2.1, U1.Control_Voltage
  N6: Q1.C, V1.V+
